# Fritzing sketch Sketch_Bengala (saved by Fritzing 0.9.3b)
breadboards: 1

parts:
  Componente2 = Arduino Nano (Rev3.0) (ICSP)
  hc-sr1 = hc-sr04
  hc-sr2 = hc-sr04
  U1 = Vibration Motor- ROB-08449 [package=vibe-motor-10mm]
  U2 = Vibration Motor- ROB-08449 [package=vibe-motor-10mm]

nets:
  N1: Componente2.D5, U2.-
  N2: Componente2.D6, U1.-
  N3: Componente2.D8, hc-sr1.Echo
  N4: Componente2.D9, hc-sr1.Trig
  N5: Componente2.D11/MOSI, hc-sr2.Echo
  N6: Componente2.D12/MISO, hc-sr2.Trig
  GND: Componente2.GND, hc-sr1.GND, hc-sr2.GND, U1.+, U2.+
  VCC: Componente2.5V, hc-sr1.VCC, hc-sr2.VCC
